// Logisim project s-mips.circ as structural Verilog
module S_MIPS_Board (
  input  DESHABILITAR_DISPATCHER,
  output halt
);

  wire button_1_out, CLK, CS, d_ff_1_q, LCLR, LoadRAM, LoadRAMOn, LW, R_R_W, R_W, ram_dispatcher_1_finished,
       RCS, Reset_out, RST, TTY_EN;
  wire [2:0] KDB;
  wire [3:0] LMask, Mask, ram_1_read_time, ram_1_write_time, RMask;
  wire [6:0] KDB_DATA, TTY_DATA;
  wire [15:0] Addr, LAddr, RAddr;
  wire [31:0] I0, I1, I2, I3, LData, ram_1_data_out_0, ram_1_data_out_1, ram_1_data_out_2, ram_1_data_out_3,
       RI0, RI1, RI2, RI3;

  TTY #(.rows(25), .cols(80)) tty_1 (.data(TTY_DATA), .clk(CLK), .we(TTY_EN), .clr(RST));
  not not_1 (LoadRAMOn, ram_dispatcher_1_finished);
  RAM_Dispatcher ram_dispatcher_1 (
    .WriteTime(ram_1_write_time), .Clock(CLK), .Data(LData), .Address(LAddr), .Mask(LMask),
    .Finished(ram_dispatcher_1_finished), .Write(LW), .CLR(LCLR));
  Keyboard #(.buflen(64)) keyboard_1 (.clk(CLK), .re(KDB[0]), .avail(KDB[2]), .data(KDB_DATA));  // open: clr
  RAM ram_1 (
    .Address(RAddr), .Data_Out_0(ram_1_data_out_0), .Data_Out_1(ram_1_data_out_1),
    .Data_Out_2(ram_1_data_out_2), .Data_Out_3(ram_1_data_out_3), .Data_In_0(RI0), .Data_In_1(RI1),
    .Data_In_2(RI2), .Data_In_3(RI3), .Mask(RMask), .nRead_Write(R_R_W), .Chip_Select(RCS),
    .Read_Time(ram_1_read_time), .Reset(button_1_out), .Write_Time(ram_1_write_time));
  Button button_1 (.out(button_1_out));
  D_Flip_Flop d_ff_1 (.clk(CLK), .D(1'b1), .Q(d_ff_1_q), .reset(Reset_out));  // open: Qn, preset, en
  Button Reset (.out(Reset_out));
  S_MIPS s_mips_1 (
    .Kbd_Enable(KDB[0]), .Address(Addr), .Kbd_Clear(KDB[1]), .Kbd_Available(KDB[2]), .RAM_In_0(I0),
    .Kbd_ASCII_Data(KDB_DATA), .RAM_In_1(I1), .TTY_Enable(TTY_EN), .RAM_In_2(I2), .RAM_In_3(I3),
    .TTY_ASCII_Data(TTY_DATA), .Reset(RST), .RAM_Out_0(ram_1_data_out_0), .Clock(CLK),
    .RAM_Out_1(ram_1_data_out_1), .Stop(halt), .RAM_Out_2(ram_1_data_out_2), .RAM_Out_3(ram_1_data_out_3),
    .Mask(Mask), .Read_Time(ram_1_read_time), .Write_Time(ram_1_write_time), .nRead_Write(R_W),
    .Chip_Select(CS));
  D_Flip_Flop d_ff_2 (.clk(CLK), .D(d_ff_1_q), .Qn(LCLR), .reset(Reset_out));  // open: Q, preset, en
  or or_1 (RST, LCLR, LoadRAM);
  Clock clock_1 (.out(CLK));
  Multiplexer #(.width(32), .enable("false")) multiplexer_1 (.in0(I0), .in1(LData), .out(RI0), .sel(LoadRAM));
  Multiplexer #(.width(32), .enable("false")) multiplexer_2 (.in0(I1), .in1(LData), .out(RI1), .sel(LoadRAM));
  Multiplexer #(.width(32), .enable("false")) multiplexer_3 (.in0(I2), .in1(LData), .out(RI2), .sel(LoadRAM));
  Multiplexer #(.width(32), .enable("false")) multiplexer_4 (.in0(I3), .in1(LData), .out(RI3), .sel(LoadRAM));
  and and_1 (LoadRAM, ~DESHABILITAR_DISPATCHER, LoadRAMOn);  // AND_Gate
  Multiplexer #(.width(16), .enable("false")) multiplexer_5 (.in0(Addr), .in1(LAddr), .out(RAddr), .sel(LoadRAM));
  Multiplexer #(.width(4), .enable("false")) multiplexer_6 (.in0(Mask), .in1(LMask), .out(RMask), .sel(LoadRAM));
  Multiplexer #(.enable("false")) multiplexer_7 (.in0(CS), .in1(LW), .out(RCS), .sel(LoadRAM));
  Multiplexer #(.enable("false")) multiplexer_8 (.in0(R_W), .in1(LW), .out(R_R_W), .sel(LoadRAM));

  // Notes on the sheet:
  //   NO MODIFICAR
  //   Keyboard
endmodule

module RAM (
  input  [15:0] Address,
  input  [31:0] Data_In_0,
  input  [31:0] Data_In_1,
  input  [31:0] Data_In_2,
  input  [31:0] Data_In_3,
  input  [3:0] Mask,
  input  nRead_Write,
  input  Chip_Select,
  input  Reset,
  output [31:0] Data_Out_0,
  output [31:0] Data_Out_1,
  output [31:0] Data_Out_2,
  output [31:0] Data_Out_3,
  output [3:0] Read_Time,
  output [3:0] Write_Time
);

  wire and_2_out, and_3_out, and_4_out, and_5_out, and_6_out, and_7_out, and_8_out, and_9_out, Changed, CLK,
       comparator_2_eq, comparator_3_eq, comparator_4_eq, comparator_5_eq, comparator_6_eq, Count,
       demultiplexer_3_out0, Idle, Idle_q, Load, Load0, Load1, nand_1_out, or_1_out, or_2_out, or_3_out,
       or_4_out, or_5_out, or_6_out, or_7_out, or_8_out, or_9_out, or_10_out, Proc_q, Update_Mem, Zero_Time;
  wire [3:0] counter_1_q, multiplexer_1_out, subtractor_1_out;
  wire [31:0] register_1_q, register_2_q, register_3_q, register_4_q, register_5_q;

  // Probe on 4'b0011
  // Probe on 4'b0010
  Multiplexer #(.width(4), .enable("false")) multiplexer_1 (
    .in0(4'b0011), .in1(4'b0010), .out(multiplexer_1_out), .sel(nRead_Write));
  or or_1 (or_1_out, Idle, Update_Mem);
  or or_2 (or_2_out, ~Chip_Select, Reset);  // OR_Gate
  Subtractor #(.width(4)) subtractor_1 (.a(multiplexer_1_out), .b(4'b0010), .out(subtractor_1_out));  // open: bin, bout
  Demultiplexer #(.enable("false")) demultiplexer_1 (.out0(Idle), .out1(Load0), .in(Idle_q), .sel(Changed));
  D_Flip_Flop u_Idle (.clk(CLK), .D(or_1_out), .Q(Idle_q), .preset(or_2_out));  // open: Qn, en, reset
  // Probe on counter_1_q
  Counter #(.width(4), .max('hf)) counter_1 (
    .load(Load), .D(subtractor_1_out), .count(Count), .Q(counter_1_q), .clk(CLK), .clr(or_3_out));  // open: carry
  or or_3 (or_3_out, ~Chip_Select, Reset);  // OR_Gate
  Comparator #(.width(4), .mode("unsigned")) comparator_1 (
    .a(4'b0000), .b(counter_1_q), .eq(Zero_Time));  // open: gt, lt
  or or_4 (or_4_out, Count, Load0, Load1);
  Register #(.width(32)) register_1 (.D(Data_In_0), .en(Chip_Select), .Q(register_1_q), .clk(CLK), .clr(or_5_out));
  or or_5 (or_5_out, ~Chip_Select, Reset);  // OR_Gate
  Register #(.width(32)) register_2 (.D(Data_In_1), .en(Chip_Select), .Q(register_2_q), .clk(CLK), .clr(or_6_out));
  or or_6 (or_6_out, ~Chip_Select, Reset);  // OR_Gate
  Register #(.width(32)) register_3 (.D(Data_In_2), .en(Chip_Select), .Q(register_3_q), .clk(CLK), .clr(or_7_out));
  or or_7 (or_7_out, ~Chip_Select, Reset);  // OR_Gate
  Register #(.width(32)) register_4 (.D(Data_In_3), .en(Chip_Select), .Q(register_4_q), .clk(CLK), .clr(or_8_out));
  or or_8 (or_8_out, ~Chip_Select, Reset);  // OR_Gate
  Register #(.width(32)) register_5 (
    .D({{11{1'b1}}, nRead_Write, Mask, Address}), .en(Chip_Select), .Q(register_5_q), .clk(CLK),
    .clr(or_9_out));
  or or_9 (or_9_out, ~Chip_Select, Reset);  // OR_Gate
  D_Flip_Flop Proc (.clk(CLK), .D(or_4_out), .Q(Proc_q), .reset(or_10_out));  // open: Qn, preset, en
  or or_10 (or_10_out, ~Chip_Select, Reset);  // OR_Gate
  Demultiplexer #(.enable("false")) demultiplexer_2 (
    .out0(Count), .out1(Update_Mem), .in(demultiplexer_3_out0), .sel(Zero_Time));
  Demultiplexer #(.enable("false")) demultiplexer_3 (
    .out0(demultiplexer_3_out0), .out1(Load1), .in(Proc_q), .sel(Changed));
  Clock clock_1 (.out(CLK));
  Comparator #(.width(32)) comparator_2 (.a(register_1_q), .b(Data_In_0), .eq(comparator_2_eq));  // open: gt, lt
  Comparator #(.width(32)) comparator_3 (.a(register_2_q), .b(Data_In_1), .eq(comparator_3_eq));  // open: gt, lt
  Comparator #(.width(32)) comparator_4 (.a(register_3_q), .b(Data_In_2), .eq(comparator_4_eq));  // open: gt, lt
  Comparator #(.width(32)) comparator_5 (.a(register_4_q), .b(Data_In_3), .eq(comparator_5_eq));  // open: gt, lt
  Comparator #(.width(32)) comparator_6 (
    .a(register_5_q), .b({{11{1'b1}}, nRead_Write, Mask, Address}), .eq(comparator_6_eq));  // open: gt, lt
  nand nand_1 (nand_1_out, comparator_6_eq, comparator_2_eq, comparator_3_eq, comparator_4_eq, comparator_5_eq);
  and and_1 (Changed, nand_1_out, Chip_Select);
  or or_11 (Load, Count, Load1, Load0);
  and and_2 (and_2_out, Mask[0], Update_Mem, nRead_Write);
  and and_3 (and_3_out, Mask[1], Update_Mem, nRead_Write);
  and and_4 (and_4_out, Mask[2], Update_Mem, nRead_Write);
  and and_5 (and_5_out, Mask[3], Update_Mem, nRead_Write);
  RAM_part #(.addrWidth(16), .dataWidth(32), .bus("separate")) ram_1 (
    .addr(Address), .din(Data_In_0), .data(Data_Out_0), .str(and_2_out), .sel(Chip_Select), .clk(CLK),
    .ld(and_6_out), .clr(Reset));
  and and_6 (and_6_out, ~nRead_Write, Idle);  // AND_Gate
  RAM_part #(.addrWidth(16), .dataWidth(32), .bus("separate")) ram_2 (
    .addr(Address), .din(Data_In_1), .data(Data_Out_1), .str(and_3_out), .sel(Chip_Select), .clk(CLK),
    .ld(and_7_out), .clr(Reset));
  and and_7 (and_7_out, ~nRead_Write, Idle);  // AND_Gate
  RAM_part #(.addrWidth(16), .dataWidth(32), .bus("separate")) ram_3 (
    .addr(Address), .din(Data_In_2), .data(Data_Out_2), .str(and_4_out), .sel(Chip_Select), .clk(CLK),
    .ld(and_8_out), .clr(Reset));
  and and_8 (and_8_out, ~nRead_Write, Idle);  // AND_Gate
  RAM_part #(.addrWidth(16), .dataWidth(32), .bus("separate")) ram_4 (
    .addr(Address), .din(Data_In_3), .data(Data_Out_3), .str(and_5_out), .sel(Chip_Select), .clk(CLK),
    .ld(and_9_out), .clr(Reset));
  and and_9 (and_9_out, ~nRead_Write, Idle);  // AND_Gate

  assign Read_Time = 4'b0011;
  assign Write_Time = 4'b0010;

  // Other names for the same wires on the sheet: M0 = Mask[0]; M1 = Mask[1]; M2 = Mask[2]; M3 = Mask[3];
  //   RW = nRead_Write; CLR = Reset; CS = Chip_Select; Load2 = Count

  // Notes on the sheet:
  //   NO MODIFICAR
  //   excepto quizás los valores RT y WT
  //   BANK0
  //   BANK1
  //   BANK2
  //   BANK3
endmodule

module S_MIPS (
  input  Kbd_Available,
  input  [6:0] Kbd_ASCII_Data,
  input  [31:0] RAM_Out_0,
  input  [31:0] RAM_Out_1,
  input  Reset,
  input  [31:0] RAM_Out_2,
  input  Clock,
  input  [31:0] RAM_Out_3,
  input  [3:0] Read_Time,
  input  [3:0] Write_Time,
  output Kbd_Enable,
  output [15:0] Address,
  output Kbd_Clear,
  output TTY_Enable,
  output [6:0] TTY_ASCII_Data,
  output Stop,
  output [31:0] RAM_In_0,
  output [31:0] RAM_In_1,
  output [31:0] RAM_In_2,
  output [31:0] RAM_In_3,
  output [3:0] Mask,
  output nRead_Write,
  output Chip_Select
);

  wire andi, beq, bgtz, blez, bltz, bne, DP_GI, get_Data, Get_Inst, i, J, Jr, KBD, lw, mfhi, mflo, or_1_out,
       ori, PC_enable, pop, push, Ready_Data, Ready_Inst, Ready_Write, rnd, Signo, Start, sw, Write, xori;
  wire [3:0] ALU_select;
  wire [4:0] RD, RS, RT;
  wire [6:0] KBD_Data_t;
  wire [15:0] Const;
  wire [25:0] Dest;
  wire [31:0] Addreess, Instruction, multiplexer_1_out, multiplexer_2_out, multiplexer_3_out,
       multiplexer_4_out, ram_interaction_1_out_14, ram_interaction_1_out_15, ram_interaction_1_out_16,
       ram_interaction_1_out_17, Write_out;

  Control_Unit___C_U control_unit_c_u_1 (
    .in_1(Instruction), .in_2(Ready_Write), .in_3(Ready_Inst), .in_4(Ready_Data), .in_5(Start), .in_6(Clock),
    .in_7(Reset), .out_13(Get_Inst), .ALU_Select(ALU_select), .out_16(Signo), .out_17(i), .out_15(PC_enable),
    .TTY_enable(TTY_Enable), .out_8(Dest), .out_9(Const), .out_10(RS), .out_11(RT), .out_12(RD),
    .out_20(pop), .out_22(mflo), .out_19(push), .out_21(mfhi), .out_23(lw), .out_24(sw), .out_25(beq),
    .out_26(bne), .out_27(blez), .out_28(bgtz), .out_29(bltz), .out_38(Kbd_Enable), .out_31(J), .out_30(Jr),
    .out_33(andi), .out_32(ori), .out_35(xori), .out_34(rnd), .out_37(KBD), .out_36(Write),
    .out_39(get_Data), .STOP(Stop));
  D_Flip_Flop #(.trigger("falling")) d_ff_1 (.clk(Clock), .D(Reset), .Q(Start));  // open: Qn, preset, en, reset
  or or_1 (or_1_out, Get_Inst, Ready_Inst);
  D_Flip_Flop #(.trigger("falling")) d_ff_2 (
    .clk(Clock), .D(Get_Inst), .Q(DP_GI), .en(or_1_out));  // open: Qn, preset, reset
  Multiplexer #(.width(32), .enable("false")) multiplexer_1 (
    .in0(RAM_Out_0), .in1(Write_out), .out(multiplexer_1_out), .sel(Write));
  Multiplexer #(.width(32), .enable("false")) multiplexer_2 (
    .in0(RAM_Out_1), .in1(Write_out), .out(multiplexer_2_out), .sel(Write));
  Multiplexer #(.width(32), .enable("false")) multiplexer_3 (
    .in0(RAM_Out_2), .in1(Write_out), .out(multiplexer_3_out), .sel(Write));
  Multiplexer #(.width(32), .enable("false")) multiplexer_4 (
    .in0(RAM_Out_3), .in1(Write_out), .out(multiplexer_4_out), .sel(Write));
  Data_Path___D_P data_path_d_p_1 (
    .in_9(DP_GI), .out_35(Addreess), .in_1(Instruction), .in_14(Clock), .in_15(Reset), .Instrucciones(push),
    .in_19(pop), .in_21(mfhi), .in_23(mflo), .in_25(rnd), .in_27(beq), .in_29(bne), .in_18(bltz),
    .in_20(andi), .in_22(ori), .in_24(xori), .in_26(sw), .in_28(lw), .in_30(Jr), .in_32(J), .in_34(KBD),
    .in_31(blez), .in_33(bgtz), .in_12(Write), .TTY_Data(TTY_ASCII_Data), .in_4(KBD_Data_t), .in_5(RS),
    .in_6(RD), .in_7(RT), .in_3(Const), .in_10(PC_enable), .in_13(nRead_Write), .in_16(i), .in_11(Signo),
    .Read_Out(Write_out), .in_2(Dest), .in_8(ALU_select));
  RAM_interaction ram_interaction_1 (
    .in_1(multiplexer_1_out), .in_2(multiplexer_2_out), .in_3(multiplexer_3_out), .in_4(multiplexer_4_out),
    .in_5(Addreess), .in_6(Read_Time), .in_7(Write_Time), .in_12(Reset), .in_11(Write), .in_9(Get_Inst),
    .in_8(get_Data), .in_10(Ready_Inst), .out_14(ram_interaction_1_out_14),
    .out_15(ram_interaction_1_out_15), .out_16(ram_interaction_1_out_16), .out_17(ram_interaction_1_out_17),
    .out_18(Address), .out_19(Mask), .out_20(Chip_Select), .out_21(nRead_Write), .out_22(Ready_Inst),
    .out_23(Ready_Data), .out_24(Ready_Write), .in_13(Clock));
  Multiplexer #(.select(2), .width(32), .enable("false")) multiplexer_5 (
    .in0(ram_interaction_1_out_14), .in1(ram_interaction_1_out_15), .in2(ram_interaction_1_out_16),
    .in3(ram_interaction_1_out_17), .out(Instruction), .sel(Addreess[3:2]));

  assign Kbd_Clear = Reset;

  // Other names for the same wires on the sheet: CLK = Clock; CS = Chip_Select; KBD_AVAIL = Kbd_Available;
  //   CLR = Reset; KBD_CLR = Reset; KBD_DATA[6:0] = Kbd_ASCII_Data; RAM_A[15:0] = Address;
  //   RAM_INPUT_0[31:0] = RAM_In_0; RAM_INPUT_1[31:0] = RAM_In_1; RAM_INPUT_2[31:0] = RAM_In_2;
  //   RAM_INPUT_3[31:0] = RAM_In_3; RAM_MASK[3:0] = Mask; RAM_OUTPUT_0[31:0] = RAM_Out_0;
  //   RAM_OUTPUT_1[31:0] = RAM_Out_1; RAM_OUTPUT_2[31:0] = RAM_Out_2; RAM_OUTPUT_3[31:0] = RAM_Out_3;
  //   RW = nRead_Write; TTY_DATA[6:0] = TTY_ASCII_Data

  // Notes on the sheet:
  //   RAM ADDRESS
  //   DATA FROM RAM
  //   DATA TO RAM
  //   DATA WRITE MASK
  //   RAM TIMING
  //   RAM CONTROL
  //   KEYBOARD
  //   TTY
  //   SEQUENCING
endmodule

module RAM_Dispatcher (
  input  [3:0] WriteTime,
  input  Clock,
  input  CLR,
  output [31:0] Data,
  output [15:0] Address,
  output [3:0] Mask,
  output Finished,
  output Write
);

  wire demultiplexer_2_out1, demultiplexer_3_out1, End, IDLE_q, IncAddr, Load, or_1_out, or_2_out, While_q,
       WriteEnd;
  wire [3:0] counter_1_q;
  wire [31:0] CurrentAddress_q;

  Counter #(.width(32), .max('hffffffff)) CurrentAddress (
    .count(IncAddr), .Q({CurrentAddress_q[31:18], Address, CurrentAddress_q[1:0]}), .clk(Clock), .clr(CLR));  // open: load, D, carry
  or or_1 (or_1_out, IncAddr, demultiplexer_3_out1, Finished);
  D_Flip_Flop IDLE (.clk(Clock), .D(or_1_out), .Q(IDLE_q), .preset(CLR));  // open: Qn, en, reset
  Demultiplexer #(.enable("false")) demultiplexer_1 (.out0(Load), .out1(Finished), .in(IDLE_q), .sel(End));
  D_Flip_Flop While (.clk(Clock), .D(or_2_out), .Q(While_q), .reset(CLR));  // open: Qn, preset, en
  or or_2 (or_2_out, Write, Load);
  RAM_part #(.addrWidth(18), .dataWidth(32)) ram_1 (
    .addr({Address, CurrentAddress_q[1:0]}), .data(Data), .clk(Clock));  // open: sel, ld, clr
  Demultiplexer #(.enable("false")) demultiplexer_2 (
    .out0(Write), .out1(demultiplexer_2_out1), .in(While_q), .sel(WriteEnd));
  Decoder #(.select(2)) decoder_1 (
    .out0(Mask[0]), .out1(Mask[1]), .out2(Mask[2]), .out3(Mask[3]), .sel(CurrentAddress_q[1:0]));  // open: en
  Demultiplexer #(.enable("false")) demultiplexer_3 (
    .out0(IncAddr), .out1(demultiplexer_3_out1), .in(demultiplexer_2_out1), .sel(End));
  Counter #(.width(4), .max('hf)) counter_1 (
    .load(Load), .D(WriteTime), .count(Write), .Q(counter_1_q), .clk(Clock));  // open: carry, clr
  Comparator #(.width(32)) comparator_1 (.a(Data), .b({32{1'b1}}), .eq(End));  // open: gt, lt
  Comparator #(.width(4)) comparator_2 (.a(4'b0000), .b(counter_1_q), .eq(WriteEnd));  // open: gt, lt

  // Other names for the same wires on the sheet: CLK = Clock; Count = Write; WT[3:0] = WriteTime
endmodule

module ALU_2 (
  input  [31:0] in_1,
  input  [31:0] in_2,
  input  [3:0] in_3,
  input  in_4,
  input  in_5,
  input  in_6,
  output [31:0] out_7,
  output [31:0] HI,
  output [31:0] Lo
);

  wire Load, Mult, mult_div_1_division;
  wire [31:0] A_B, And, D_HI, D_Lo, M_HI, M_Lo, multiplexer_1_out, multiplexer_2_out, Nand, Nor, Or, Resta,
       Suma, Xor;

  Mult_Div mult_div_1 (.in_1(in_3), .Multiplicacion(Mult), .Division(mult_div_1_division));
  or or_1 (Load, Mult, mult_div_1_division);
  assign And = in_1 & in_2;  // AND_Gate and_1, 32 bits wide
  assign Or = in_1 | in_2;  // OR_Gate or_2, 32 bits wide
  assign Nand = ~(in_1 & in_2);  // NAND_Gate nand_1, 32 bits wide
  assign Nor = ~(in_1 | in_2);  // NOR_Gate nor_1, 32 bits wide
  assign Xor = in_1 ^ in_2;  // XOR_Gate xor_1, 32 bits wide
  Adder #(.width(32)) adder_1 (.a(in_1), .b(in_2), .out(Suma));  // open: cin, cout
  Subtractor #(.width(32)) subtractor_1 (.a(in_1), .b(in_2), .out(Resta));  // open: bin, bout
  Comparar comparar_1 (.in_1(in_1), .in_2(in_2), .in_3(in_4), .out_4(A_B));
  Multiplicar multiplicar_1 (.in_1(in_1), .in_2(in_2), .in_3(in_4), .out_4(M_HI), .out_5(M_Lo));
  Dividir dividir_1 (.in_1(in_1), .in_2(in_2), .in_3(in_4), .out_4(D_HI), .out_5(D_Lo));
  Multiplexer #(.width(32), .enable("false")) multiplexer_1 (
    .in0(D_HI), .in1(M_HI), .out(multiplexer_1_out), .sel(Mult));
  Multiplexer #(.width(32), .enable("false")) multiplexer_2 (
    .in0(M_Lo), .in1(D_Lo), .out(multiplexer_2_out), .sel(Mult));
  Multiplexer #(.select(4), .width(32), .enable("false")) multiplexer_3 (
    .in0(Suma), .in1(Resta), .in4(A_B), .in5(And), .in6(Or), .in7(Nand), .in8(Nor), .in9(Xor), .out(out_7),
    .sel(in_3));  // open: in2, in3, in10, in11, in12, in13, in14, in15
  Register #(.width(32)) register_1 (.D(multiplexer_1_out), .en(Load), .Q(HI), .clk(in_5), .clr(in_6));
  Register #(.width(32)) register_2 (.D(multiplexer_2_out), .en(Load), .Q(Lo), .clk(in_5), .clr(in_6));

  // Other names for the same wires on the sheet: A[31:0] = in_1; B[31:0] = in_2; CLK = in_5; CLR = in_6;
  //   Ope_Select[3:0] = in_3; Signo = in_4

  // Notes on the sheet:
  //   Ver si la operacion es de multiplicar o de dividir
endmodule

module ALU_Selector (
  input  in_1,
  input  in_2,
  input  in_3,
  input  in_4,
  input  in_5,
  input  in_6,
  input  in_7,
  input  in_8,
  input  in_9,
  input  in_10,
  input  in_11,
  input  in_12,
  input  in_13,
  input  in_14,
  input  in_15,
  input  in_16,
  input  in_17,
  input  in_18,
  output [3:0] Selector,
  output Signo,
  output I
);

  wire AND, DIV, MUL, OR, SLT, SLTI;

  or or_1 (MUL, in_3, in_4);
  or or_2 (DIV, in_5, in_6);
  or or_3 (SLT, in_7, in_8);
  or or_4 (SLTI, in_14, in_15);
  or or_5 (AND, in_9, in_16);
  or or_6 (OR, in_10, in_17);
  or or_7 (Selector[3], in_12, in_18);
  or or_8 (Selector[0], in_2, DIV, AND, in_11);
  or or_9 (Selector[1], MUL, DIV, in_11, OR);
  or or_10 (Selector[2], SLT, SLTI, AND, in_11, OR);
  or or_11 (Signo, in_4, in_6, in_8, in_15);
  or or_12 (I, in_13, in_14, in_16, in_17, in_18);

  // Other names for the same wires on the sheet: Add = in_1; Addi = in_13; And_t = in_9; Andi = in_16; Div_t = in_5;
  //   Divu = in_6; Mul_t = in_3; Mulu = in_4; Nor = in_11; Or_t = in_10; Ori = in_17; _0 = Selector[0];
  //   _1 = Selector[1]; _2 = Selector[2]; _3 = Selector[3]; XOR = Selector[3]; Slt_t = in_7; Slti_t = in_14;
  //   Sltiu = in_15; Sltu = in_8; Sub = in_2; Xor_t = in_12; Xori = in_18
endmodule

module Mult_Div (
  input  [3:0] in_1,
  output Multiplicacion,
  output Division
);

  and and_1 (Multiplicacion, ~in_1[0], in_1[1], ~in_1[2], ~in_1[3]);  // AND_Gate
  and and_2 (Division, in_1[0], in_1[1], ~in_1[2], ~in_1[3]);  // AND_Gate
endmodule

module Comparar (
  input  [31:0] in_1,
  input  [31:0] in_2,
  input  in_3,
  output [31:0] out_4
);

  wire comparator_1_lt, comparator_2_lt, multiplexer_1_out;

  Comparator #(.width(32), .mode("unsigned")) comparator_1 (.a(in_1), .b(in_2), .lt(comparator_1_lt));  // open: gt, eq
  Multiplexer #(.enable("false")) multiplexer_1 (
    .in0(comparator_1_lt), .in1(comparator_2_lt), .out(multiplexer_1_out), .sel(in_3));
  Comparator #(.width(32)) comparator_2 (.a(in_1), .b(in_2), .lt(comparator_2_lt));  // open: gt, eq
  assign out_4 = {{31{1'b0}}, multiplexer_1_out};  // Bit_Extender bit_extender_1

  // Other names for the same wires on the sheet: A[31:0] = in_1; B[31:0] = in_2; Signo = in_3
endmodule

module Multiplicar (
  input  [31:0] in_1,
  input  [31:0] in_2,
  input  in_3,
  output [31:0] out_4,
  output [31:0] out_5
);

  wire adder_1_cout, adder_3_cout, adder_5_cout, and_1_out, c_A, c_B, rotar_izquierda_3_out_4,
       rotar_izquierda_5_out_4;
  wire [31:0] A_2, A_cB, adder_1_out, adder_2_out, adder_3_out, adder_4_out, and_2_out, and_3_out, B_2, B_cA,
       bit_extender_1_out, bit_extender_2_out, c_AB, HI_1, HI_2, LO_1, LO_2, multiplier_2_cout,
       multiplier_2_out, rotar_izquierda_3__2x_y, rotar_izquierda_4__2x_y, rotar_izquierda_5__2x_y,
       rotar_izquierda_6__2x_y;

  and and_1 (and_1_out, c_A, c_B);
  assign bit_extender_1_out = {{31{c_B}}, c_B};  // Bit_Extender bit_extender_1
  assign bit_extender_2_out = {{31{c_A}}, c_A};  // Bit_Extender bit_extender_2
  assign c_AB = {{31{1'b0}}, and_1_out};  // Bit_Extender bit_extender_3
  assign and_2_out = A_2 & bit_extender_1_out;  // AND_Gate and_2, 32 bits wide
  assign and_3_out = B_2 & bit_extender_2_out;  // AND_Gate and_3, 32 bits wide
  Rotar_Izquierda rotar_izquierda_1 (.X(and_2_out), ._2X_Y(A_cB), .Y(1'b0));  // open: out_4
  Rotar_Izquierda rotar_izquierda_2 (.X(and_3_out), ._2X_Y(B_cA), .Y(1'b0));  // open: out_4
  Multiplier #(.width(32)) multiplier_1 (.a(in_1), .b(in_2), .out(LO_1), .cout(HI_1));  // open: cin
  Multiplier #(.width(32)) multiplier_2 (
    .a(A_2), .b(B_2), .out(multiplier_2_out), .cout(multiplier_2_cout));  // open: cin
  Rotar_Izquierda rotar_izquierda_3 (
    .X(multiplier_2_out), ._2X_Y(rotar_izquierda_3__2x_y), .Y(1'b0), .out_4(rotar_izquierda_3_out_4));
  Rotar_Izquierda rotar_izquierda_4 (
    .X(multiplier_2_cout), ._2X_Y(rotar_izquierda_4__2x_y), .Y(rotar_izquierda_3_out_4));  // open: out_4
  Rotar_Derecha rotar_derecha_1 (.X(in_1), .X_2(c_A), .in_2(1'b0), .X_2_2(A_2));
  Rotar_Izquierda rotar_izquierda_5 (
    .X(rotar_izquierda_3__2x_y), ._2X_Y(rotar_izquierda_5__2x_y), .Y(1'b0), .out_4(rotar_izquierda_5_out_4));
  Rotar_Izquierda rotar_izquierda_6 (
    .X(rotar_izquierda_4__2x_y), ._2X_Y(rotar_izquierda_6__2x_y), .Y(rotar_izquierda_5_out_4));  // open: out_4
  Rotar_Derecha rotar_derecha_2 (.X(in_2), .X_2(c_B), .in_2(1'b0), .X_2_2(B_2));
  Adder #(.width(32)) adder_1 (
    .a(rotar_izquierda_5__2x_y), .b(A_cB), .out(adder_1_out), .cin(1'b0), .cout(adder_1_cout));
  Adder #(.width(32)) adder_2 (
    .a(rotar_izquierda_6__2x_y), .b({32{1'b0}}), .out(adder_2_out), .cin(adder_1_cout));  // open: cout
  Adder #(.width(32)) adder_3 (.a(adder_1_out), .b(B_cA), .out(adder_3_out), .cin(1'b0), .cout(adder_3_cout));
  Adder #(.width(32)) adder_4 (.a(adder_2_out), .b({32{1'b0}}), .out(adder_4_out), .cin(adder_3_cout));  // open: cout
  Adder #(.width(32)) adder_5 (.a(adder_3_out), .b(c_AB), .out(LO_2), .cin(1'b0), .cout(adder_5_cout));
  Adder #(.width(32)) adder_6 (.a(adder_4_out), .b({32{1'b0}}), .out(HI_2), .cin(adder_5_cout));  // open: cout
  Multiplexer #(.width(32), .enable("false")) multiplexer_1 (.in0(HI_1), .in1(HI_2), .out(out_4), .sel(in_3));
  Multiplexer #(.width(32), .enable("false")) multiplexer_2 (.in0(LO_1), .in1(LO_2), .out(out_5), .sel(in_3));

  // Other names for the same wires on the sheet: A[31:0] = in_1; B[31:0] = in_2; Signo = in_3
endmodule

module Rotar_Izquierda (
  input  Y,
  input  [31:0] X,
  output [31:0] _2X_Y,
  output out_4
);


  assign _2X_Y = {X[30:0], Y};
  assign out_4 = X[31];
endmodule

module Rotar_Derecha (
  input  [31:0] X,
  input  in_2,
  output X_2,
  output [31:0] X_2_2
);


  assign X_2 = X[0];
  assign X_2_2 = {in_2, X[31:1]};
endmodule

module Dividir (
  input  [31:0] in_1,
  input  [31:0] in_2,
  input  in_3,
  output [31:0] out_4,
  output [31:0] out_5
);

  wire Neg_A, Neg_B, Neg_Div;
  wire [31:0] A_t, adder_1_out, B_t, divider_1_out, multiplexer_1_out, negator_1_out, negator_2_out,
       negator_3_out, R, subtractor_1_out;

  and and_1 (Neg_A, in_1[31], in_3);
  and and_2 (Neg_B, in_3, in_2[31]);
  Divider #(.width(32)) divider_1 (.a(A_t), .b(B_t), .out(divider_1_out), .rem(R));  // open: upper
  xor xor_1 (Neg_Div, Neg_A, Neg_B);
  Adder #(.width(32)) adder_1 (.a(divider_1_out), .b(32'h1), .out(adder_1_out));  // open: cin, cout
  Subtractor #(.width(32)) subtractor_1 (.a(B_t), .b(R), .out(subtractor_1_out));  // open: bin, bout
  Multiplexer #(.width(32), .enable("false")) multiplexer_1 (
    .in0(divider_1_out), .in1(adder_1_out), .out(multiplexer_1_out), .sel(Neg_A));
  Multiplexer #(.width(32), .enable("false")) multiplexer_2 (.in0(R), .in1(subtractor_1_out), .out(out_4), .sel(Neg_A));
  Negator #(.width(32)) negator_1 (.in(in_1), .out(negator_1_out));
  Negator #(.width(32)) negator_2 (.in(in_2), .out(negator_2_out));
  Negator #(.width(32)) negator_3 (.in(multiplexer_1_out), .out(negator_3_out));
  Multiplexer #(.width(32), .enable("false")) multiplexer_3 (.in0(in_1), .in1(negator_1_out), .out(A_t), .sel(Neg_A));
  Multiplexer #(.width(32), .enable("false")) multiplexer_4 (.in0(in_2), .in1(negator_2_out), .out(B_t), .sel(Neg_B));
  Multiplexer #(.width(32), .enable("false")) multiplexer_5 (
    .in0(multiplexer_1_out), .in1(negator_3_out), .out(out_5), .sel(Neg_Div));

  // Other names for the same wires on the sheet: A[31:0] = in_1; A_B[31:0] = out_4; A_B_t[31:0] = out_5;
  //   B[31:0] = in_2; Signo = in_3
endmodule

module Register_File (
  input  [31:0] in_1,
  input  [4:0] in_2,
  input  [4:0] in_3,
  input  [4:0] in_4,
  input  in_5,
  input  in_6,
  input  in_7,
  input  in_8,
  input  in_9,
  input  in_10,
  output [31:0] A,
  output [31:0] B,
  output [31:0] SP
);

  wire and_1_out, L_0, L_1, L_2, L_3, L_4, L_5, L_6, L_7, L_8, L_9, L_10, L_11, L_12, L_13, L_14, L_15, L_16,
       L_17, L_18, L_19, L_20, L_21, L_22, L_23, L_24, L_25, L_26, L_27, L_28, L_29, L_30, L_31, L_31_1,
       or_1_out;
  wire [31:0] adder_1_out, In_SP, multiplexer_1_out, multiplexer_2_out, Out_0, Out_1, Out_2, Out_3, Out_4,
       Out_5, Out_6, Out_7, Out_8, Out_9, Out_10, Out_11, Out_12, Out_13, Out_14, Out_15, Out_16, Out_17,
       Out_18, Out_19, Out_20, Out_21, Out_22, Out_23, Out_24, Out_25, Out_26, Out_27, Out_28, Out_29,
       Out_30, Out_31, subtractor_1_out;

  Demultiplexer #(.select(5), .enable("false")) demultiplexer_1 (
    .out0(L_0), .out1(L_1), .out2(L_2), .out3(L_3), .out4(L_4), .out5(L_5), .out6(L_6), .out7(L_7),
    .out8(L_8), .out9(L_9), .out10(L_10), .out11(L_11), .out12(L_12), .out13(L_13), .out14(L_14),
    .out15(L_15), .out16(L_16), .out17(L_17), .out18(L_18), .out19(L_19), .out20(L_20), .out21(L_21),
    .out22(L_22), .out23(L_23), .out24(L_24), .out25(L_25), .out26(L_26), .out27(L_27), .out28(L_28),
    .out29(L_29), .out30(L_30), .out31(L_31_1), .in(in_6), .sel(in_2));
  or or_1 (or_1_out, in_7, in_8);
  and and_1 (and_1_out, or_1_out, in_5);
  or or_2 (L_31, and_1_out, in_10, L_31_1);
  Register #(.width(32)) register_1 (.D({32{1'b0}}), .en(L_0), .Q(Out_0), .clk(in_9), .clr(in_10));
  Register #(.width(32)) register_2 (.D(in_1), .en(L_4), .Q(Out_4), .clk(in_9), .clr(in_10));
  Register #(.width(32)) register_3 (.D(in_1), .en(L_8), .Q(Out_8), .clk(in_9), .clr(in_10));
  Register #(.width(32)) register_4 (.D(in_1), .en(L_12), .Q(Out_12), .clk(in_9), .clr(in_10));
  Register #(.width(32)) register_5 (.D(in_1), .en(L_16), .Q(Out_16), .clk(in_9), .clr(in_10));
  Register #(.width(32)) register_6 (.D(in_1), .en(L_20), .Q(Out_20), .clk(in_9), .clr(in_10));
  Register #(.width(32)) register_7 (.D(in_1), .en(L_24), .Q(Out_24), .clk(in_9), .clr(in_10));
  Register #(.width(32)) register_8 (.D(in_1), .en(L_28), .Q(Out_28), .clk(in_9), .clr(in_10));
  Adder #(.width(32)) adder_1 (.a(SP), .b(32'h4), .out(adder_1_out));  // open: cin, cout
  Subtractor #(.width(32)) subtractor_1 (.a(SP), .b(32'h4), .out(subtractor_1_out));  // open: bin, bout
  Register #(.width(32)) register_9 (.D(in_1), .en(L_1), .Q(Out_1), .clk(in_9), .clr(in_10));
  Register #(.width(32)) register_10 (.D(in_1), .en(L_5), .Q(Out_5), .clk(in_9), .clr(in_10));
  Register #(.width(32)) register_11 (.D(in_1), .en(L_9), .Q(Out_9), .clk(in_9), .clr(in_10));
  Register #(.width(32)) register_12 (.D(in_1), .en(L_13), .Q(Out_13), .clk(in_9), .clr(in_10));
  Register #(.width(32)) register_13 (.D(in_1), .en(L_17), .Q(Out_17), .clk(in_9), .clr(in_10));
  Register #(.width(32)) register_14 (.D(in_1), .en(L_21), .Q(Out_21), .clk(in_9), .clr(in_10));
  Register #(.width(32)) register_15 (.D(in_1), .en(L_25), .Q(Out_25), .clk(in_9), .clr(in_10));
  Register #(.width(32)) register_16 (.D(in_1), .en(L_29), .Q(Out_29), .clk(in_9), .clr(in_10));
  Multiplexer #(.width(32), .enable("false")) multiplexer_1 (
    .in0(adder_1_out), .in1(subtractor_1_out), .out(multiplexer_1_out), .sel(in_7));
  Register #(.width(32)) register_17 (.D(in_1), .en(L_2), .Q(Out_2), .clk(in_9), .clr(in_10));
  Register #(.width(32)) register_18 (.D(in_1), .en(L_6), .Q(Out_6), .clk(in_9), .clr(in_10));
  Register #(.width(32)) register_19 (.D(in_1), .en(L_10), .Q(Out_10), .clk(in_9), .clr(in_10));
  Register #(.width(32)) register_20 (.D(in_1), .en(L_14), .Q(Out_14), .clk(in_9), .clr(in_10));
  Register #(.width(32)) register_21 (.D(in_1), .en(L_18), .Q(Out_18), .clk(in_9), .clr(in_10));
  Register #(.width(32)) register_22 (.D(in_1), .en(L_22), .Q(Out_22), .clk(in_9), .clr(in_10));
  Register #(.width(32)) register_23 (.D(in_1), .en(L_26), .Q(Out_26), .clk(in_9), .clr(in_10));
  Register #(.width(32)) register_24 (.D(in_1), .en(L_30), .Q(Out_30), .clk(in_9), .clr(in_10));
  Multiplexer #(.width(32), .enable("false")) multiplexer_2 (
    .in0(multiplexer_1_out), .in1({32{1'b0}}), .out(multiplexer_2_out), .sel(in_10));
  Multiplexer #(.width(32), .enable("false")) multiplexer_3 (
    .in0(multiplexer_2_out), .in1(in_1), .out(In_SP), .sel(L_31_1));
  Register #(.width(32)) register_25 (.D(in_1), .en(L_3), .Q(Out_3), .clk(in_9), .clr(in_10));
  Register #(.width(32)) register_26 (.D(in_1), .en(L_7), .Q(Out_7), .clk(in_9), .clr(in_10));
  Register #(.width(32)) register_27 (.D(in_1), .en(L_11), .Q(Out_11), .clk(in_9), .clr(in_10));
  Register #(.width(32)) register_28 (.D(in_1), .en(L_15), .Q(Out_15), .clk(in_9), .clr(in_10));
  Register #(.width(32)) register_29 (.D(in_1), .en(L_19), .Q(Out_19), .clk(in_9), .clr(in_10));
  Register #(.width(32)) register_30 (.D(in_1), .en(L_23), .Q(Out_23), .clk(in_9), .clr(in_10));
  Register #(.width(32)) register_31 (.D(in_1), .en(L_27), .Q(Out_27), .clk(in_9), .clr(in_10));
  Register #(.width(32)) register_32 (.D(In_SP), .en(L_31), .Q(SP), .clk(in_9), .clr(in_10));
  Multiplexer #(.select(5), .width(32), .enable("false")) multiplexer_4 (
    .in0(Out_0), .in1(Out_1), .in2(Out_2), .in3(Out_3), .in4(Out_4), .in5(Out_5), .in6(Out_6), .in7(Out_7),
    .in8(Out_8), .in9(Out_9), .in10(Out_10), .in11(Out_11), .in12(Out_12), .in13(Out_13), .in14(Out_14),
    .in15(Out_15), .in16(Out_16), .in17(Out_17), .in18(Out_18), .in19(Out_19), .in20(Out_20), .in21(Out_21),
    .in22(Out_22), .in23(Out_23), .in24(Out_24), .in25(Out_25), .in26(Out_26), .in27(Out_27), .in28(Out_28),
    .in29(Out_29), .in30(Out_30), .in31(Out_31), .out(A), .sel(in_3));
  Multiplexer #(.select(5), .width(32), .enable("false")) multiplexer_5 (
    .in0(Out_0), .in1(Out_1), .in2(Out_2), .in3(Out_3), .in4(Out_4), .in5(Out_5), .in6(Out_6), .in7(Out_7),
    .in8(Out_8), .in9(Out_9), .in10(Out_10), .in11(Out_11), .in12(Out_12), .in13(Out_13), .in14(Out_14),
    .in15(Out_15), .in16(Out_16), .in17(Out_17), .in18(Out_18), .in19(Out_19), .in20(Out_20), .in21(Out_21),
    .in22(Out_22), .in23(Out_23), .in24(Out_24), .in25(Out_25), .in26(Out_26), .in27(Out_27), .in28(Out_28),
    .in29(Out_29), .in30(Out_30), .in31(Out_31), .out(B), .sel(in_4));

  // Other names for the same wires on the sheet: CLK = in_9; CLR = in_10; INPUT[31:0] = in_1; Out_SP[31:0] = SP;
  //   Pop = in_8; Push = in_7; R_W = in_5; Select[4:0] = in_2; Select_A[4:0] = in_3; Select_B[4:0] = in_4;
  //   Write = in_6
endmodule

module RF_INPUT__RF_S (
  input  [31:0] in_1,
  input  [31:0] in_2,
  input  [31:0] in_3,
  input  [31:0] in_4,
  input  [31:0] in_5,
  input  [6:0] in_6,
  input  in_7,
  input  in_8,
  input  in_9,
  input  in_10,
  input  in_11,
  input  in_12,
  output [31:0] out_13
);

  wire [2:0] Select;

  Multiplexer #(.select(3), .width(32), .enable("false")) multiplexer_1 (
    .in0(in_5), .in1(in_3), .in2(in_1), .in3(in_2), .in4(in_4), .in5({{25{1'b0}}, in_6}), .out(out_13),
    .sel(Select));  // open: in6, in7
  or or_1 (Select[0], in_8, in_10, in_11, in_12);
  or or_2 (Select[1], in_7, in_8);
  or or_3 (Select[2], in_9, in_10);

  // Other names for the same wires on the sheet: ALU_Result[31:0] = in_5; HI[31:0] = in_1; Instruction[31:0] = in_3;
  //   kbd = in_10; KBD_Data[6:0] = in_6; LO[31:0] = in_2; lw = in_12; mfhi = in_7; mflo = in_8; pop = in_11;
  //   Random__RND[31:0] = in_4; rnd = in_9
endmodule

module Data_Path___D_P (
  input  [31:0] in_1,
  input  [25:0] in_2,
  input  [15:0] in_3,
  input  [6:0] in_4,
  input  [4:0] in_5,
  input  [4:0] in_6,
  input  [4:0] in_7,
  input  [3:0] in_8,
  input  in_9,
  input  in_10,
  input  in_11,
  input  in_12,
  input  in_13,
  input  in_14,
  input  in_15,
  input  in_16,
  input  Instrucciones,
  input  in_18,
  input  in_19,
  input  in_20,
  input  in_21,
  input  in_22,
  input  in_23,
  input  in_24,
  input  in_25,
  input  in_26,
  input  in_27,
  input  in_28,
  input  in_29,
  input  in_30,
  input  in_31,
  input  in_32,
  input  in_33,
  input  in_34,
  output [31:0] out_35,
  output [31:0] Read_Out,
  output [6:0] TTY_Data
);

  wire and_1_out;
  wire [4:0] RF_select;
  wire [31:0] ALU_result, branch_control_1_out_13, HI, Lo, multiplexer_1_out, Pc, Random,
       rf_input_rf_s_1_out_13, RT_t, SP;
  wire [31:7] RS_t;
  wire [31:16] X;

  Branch_Control branch_control_1 (
    .in_1(in_2), .in_2({RS_t, TTY_Data}), .in_3(RT_t), .in_4(Pc), .in_5(in_3), .in_6(in_27), .in_7(in_29),
    .in_8(in_31), .in_9(in_33), .in_10(in_18), .in_11(in_30), .in_12(in_32), .out_13(branch_control_1_out_13));
  RF_INPUT__RF_S rf_input_rf_s_1 (
    .in_1(HI), .in_2(Lo), .in_3(in_1), .in_4(Random), .in_5(ALU_result), .in_6(in_4), .in_7(in_21),
    .in_8(in_23), .in_9(in_25), .in_10(in_34), .in_11(in_19), .in_12(in_28), .out_13(rf_input_rf_s_1_out_13));
  Program_Counter__PC program_counter_pc_1 (
    .Proxima_Direccion_a_leer(branch_control_1_out_13), .Direccion_Actual(Pc), .Load(in_10), .CLK(in_14),
    .CLR(in_15));
  Register_File register_file_1 (
    .in_1(rf_input_rf_s_1_out_13), .in_2(RF_select), .in_3(in_5), .in_4(in_7), .in_5(in_13), .in_6(in_12),
    .in_7(Instrucciones), .in_8(in_19), .in_9(in_14), .in_10(in_15), .A({RS_t, TTY_Data}), .B(RT_t), .SP(SP));
  Memory_Address memory_address_1 (
    .in_1(ALU_result), .in_2(Pc), .in_3(SP), .in_4(in_19), .in_5(Instrucciones), .in_6(in_28), .in_7(in_26),
    .in_8(in_9), .out_9(out_35));
  Multiplexer #(.width(32), .enable("false")) multiplexer_1 (
    .in0(RT_t), .in1({X, in_3}), .out(multiplexer_1_out), .sel(in_16));
  ALU_2 alu_1 (
    .in_1({RS_t, TTY_Data}), .in_2(multiplexer_1_out), .in_3(in_8), .in_4(in_11), .in_5(in_14), .in_6(in_15),
    .out_7(ALU_result), .HI(HI), .Lo(Lo));
  and and_1 (and_1_out, in_3[15], ~in_20, ~in_24, ~in_22);  // AND_Gate
  Random #(.width(32)) random_1 (.clk(in_14), .next(in_25), .out(Random));  // open: clr
  Multiplexer #(.width(5), .enable("false")) multiplexer_2 (.in0(in_6), .in1(in_7), .out(RF_select), .sel(in_16));
  Bit_Extender #(.in_width(1), .\type ("input")) bit_extender_1 (.in(and_1_out), .out(X));  // open: extend
  Multiplexer #(.width(32), .enable("false")) multiplexer_3 (
    .in0({RS_t, TTY_Data}), .in1(RT_t), .out(Read_Out), .sel(in_13));

  // Other names for the same wires on the sheet: Addreess[31:0] = out_35; ALU_select[3:0] = in_8; andi = in_20;
  //   beq = in_27; bgtz = in_33; blez = in_31; bltz = in_18; bne = in_29; CLK = in_14; CLR = in_15; Dest[25:0] = in_2;
  //   Get_Instruction = in_9; I = in_16; Instruction[31:0] = in_1; j = in_32; jr = in_30; Kbd = in_34;
  //   KBD_Data[6:0] = in_4; Lw = in_28; Mfhi = in_21; Mflo = in_23; ori = in_22; Pc_enable = in_10; Pop = in_19;
  //   Push = Instrucciones; R_W = in_13; RD[4:0] = in_6; Rnd = in_25; RS[4:0] = in_5; RS_t[6:0] = TTY_Data;
  //   RT[4:0] = in_7; Signo = in_11; Sw = in_26; Write = in_12; Const[15:0] = in_3; X[15:0] = in_3; xori = in_24
endmodule

module Program_Counter__PC (
  input  [31:0] Proxima_Direccion_a_leer,
  input  Load,
  input  CLK,
  input  CLR,
  output [31:0] Direccion_Actual
);

  Register #(.width(32)) register_1 (
    .D(Proxima_Direccion_a_leer), .en(Load), .Q(Direccion_Actual), .clk(CLK), .clr(CLR));
endmodule

module Branch_Control (
  input  [25:0] in_1,
  input  [31:0] in_2,
  input  [31:0] in_3,
  input  [31:0] in_4,
  input  [15:0] in_5,
  input  in_6,
  input  in_7,
  input  in_8,
  input  in_9,
  input  in_10,
  input  in_11,
  input  in_12,
  output [31:0] out_13
);

  wire and_1_out, and_2_out, and_3_out, and_4_out, and_5_out, comparator_2_eq, ji, RS__0, RS___0, RT____RT;
  wire [1:0] Select;
  wire [13:0] bit_extender_1_out;
  wire [31:0] PC_4, PC_Constante_4;

  Adder #(.width(32)) adder_1 (.a(in_4), .b(32'h4), .out(PC_4));  // open: cin, cout
  assign bit_extender_1_out = {{13{in_5[15]}}, in_5[15]};  // Bit_Extender bit_extender_1
  Comparator #(.width(32)) comparator_1 (.a(in_3), .b(in_2), .eq(RT____RT));  // open: gt, lt
  Comparator #(.width(32)) comparator_2 (.a(in_2), .b({32{1'b0}}), .eq(comparator_2_eq), .lt(RS__0));  // open: gt
  and and_1 (and_1_out, in_6, RT____RT);
  and and_2 (and_2_out, ~RT____RT, in_7);  // AND_Gate
  and and_3 (and_3_out, in_8, RS___0);
  and and_4 (and_4_out, ~RS___0, in_9);  // AND_Gate
  and and_5 (and_5_out, RS__0, in_10);
  or or_1 (RS___0, comparator_2_eq, RS__0);
  or or_2 (ji, and_1_out, and_2_out, and_3_out, and_4_out, and_5_out);
  Adder #(.width(32)) adder_2 (
    .a(PC_4), .b({bit_extender_1_out, in_5, 2'b00}), .out(PC_Constante_4));  // open: cin, cout
  or or_3 (Select[0], in_11, ji);
  or or_4 (Select[1], in_11, in_12);
  Multiplexer #(.select(2), .width(32), .enable("false")) multiplexer_1 (
    .in0(PC_4), .in1(PC_Constante_4), .in2({in_4[31:28], in_1, 2'b00}), .in3(in_2), .out(out_13), .sel(Select));

  // Other names for the same wires on the sheet: Const[15:0] = in_5; beq = in_6; bgtz = in_9; blez = in_8;
  //   bltz = in_10; bne = in_7; j = in_12; jr = in_11; Destino[25:0] = in_1; jump[31:2] = {in_4[31:28], in_1};
  //   PC[31:0] = in_4; RS[31:0] = in_2; RT[31:0] = in_3
endmodule

module Memory_Address (
  input  [31:0] in_1,
  input  [31:0] in_2,
  input  [31:0] in_3,
  input  in_4,
  input  in_5,
  input  in_6,
  input  in_7,
  input  in_8,
  output [31:0] out_9
);

  wire [1:0] Select;
  wire [31:0] multiplexer_1_out, SP__4;

  Multiplexer #(.width(32), .enable("false")) multiplexer_1 (
    .in0(in_3), .in1(SP__4), .out(multiplexer_1_out), .sel(in_5));
  Multiplexer #(.select(2), .width(32), .enable("false")) multiplexer_2 (
    .in0(in_2), .in1(in_1), .in2(multiplexer_1_out), .in3(in_2), .out(out_9), .sel(Select));
  or or_1 (Select[0], in_6, in_7, in_8);
  or or_2 (Select[1], in_8, in_5, in_4);
  Subtractor #(.width(32)) subtractor_1 (.a(in_3), .b(32'h4), .out(SP__4));  // open: bin, bout

  // Other names for the same wires on the sheet: ALU_Result[31:0] = in_1; get_inst = in_8; lw = in_6; PC[31:0] = in_2;
  //   pop = in_4; push = in_5; SP[31:0] = in_3; sw = in_7
endmodule

module Control_Unit___C_U (
  input  [31:0] in_1,
  input  in_2,
  input  in_3,
  input  in_4,
  input  in_5,
  input  in_6,
  input  in_7,
  output [25:0] out_8,
  output [15:0] out_9,
  output [4:0] out_10,
  output [4:0] out_11,
  output [4:0] out_12,
  output out_13,
  output [3:0] ALU_Select,
  output out_15,
  output out_16,
  output out_17,
  output TTY_enable,
  output out_19,
  output out_20,
  output out_21,
  output out_22,
  output out_23,
  output out_24,
  output out_25,
  output out_26,
  output out_27,
  output out_28,
  output out_29,
  output out_30,
  output out_31,
  output out_32,
  output out_33,
  output out_34,
  output out_35,
  output out_36,
  output out_37,
  output out_38,
  output out_39,
  output STOP
);

  wire Add, Addi, ALU_Inst, And, Branch, d_ff_1_q, d_ff_2_q, d_ff_3_q, d_ff_4_q, Div, Divu, halt, Junp_Inst,
       memory_inst, Mul, Mulu, nop, Nor, Or, R_Inst, RF, RF_enable, Seguir, Slt, Slti, Sltiu, Sltu,
       stack_inst, Sub, tty, write_inst, Xor;
  wire [2:0] Select;
  wire [31:0] get_instruction_get_inst_1_out_5;

  Get_Instruction___Get_Inst get_instruction_get_inst_1 (
    .in_1(in_1), .out_5(get_instruction_get_inst_1_out_5), .Load(in_3), .CLK(in_6), .CLR(in_7));
  D_Flip_Flop #(.trigger("falling")) d_ff_1 (.clk(in_6), .D(in_5), .Q(d_ff_1_q), .reset(in_7));  // open: Qn, preset, en
  D_Flip_Flop #(.trigger("falling")) d_ff_2 (
    .clk(in_6), .D(out_15), .Q(d_ff_2_q), .reset(in_7));  // open: Qn, preset, en
  D_Flip_Flop #(.trigger("falling")) d_ff_3 (
    .clk(in_6), .D(Seguir), .Q(d_ff_3_q), .reset(in_7));  // open: Qn, preset, en
  or or_1 (ALU_Inst, Add, Addi, Sub, Mul, Mulu, Div, Divu, Slt, Sltu, Slti, Sltiu, And, out_33, Or, out_32, Nor, Xor, out_35);
  or or_2 (out_13, d_ff_1_q, d_ff_2_q);
  or or_3 (Junp_Inst, nop, out_26, out_25, out_27, out_28, out_29, out_30, out_31);
  or or_4 (R_Inst, out_21, out_22, out_37, out_34, tty);
  or or_5 (RF_enable, d_ff_3_q, in_4, RF);
  or or_6 (stack_inst, out_20, out_19);
  or or_7 (write_inst, out_19, out_24);
  or or_8 (memory_inst, out_24, out_23);
  D_Flip_Flop #(.trigger("falling")) d_ff_4 (.clk(in_6), .D(in_4), .Q(d_ff_4_q), .reset(in_7));  // open: Qn, preset, en
  D_Flip_Flop #(.trigger("falling")) d_ff_5 (
    .clk(in_6), .D(RF_enable), .Q(out_38), .reset(in_7));  // open: Qn, preset, en
  Demultiplexer #(.select(3), .enable("false")) demultiplexer_1 (
    .out0(STOP), .out1(Seguir), .out2(Branch), .out3(RF), .out4(out_39), .out5(out_36), .in(d_ff_4_q),
    .sel(Select));  // open: out6, out7
  or or_9 (out_15, out_38, in_2, Branch);
  instruction_decoder instruction_decoder_1 (
    .Output(out_10), .Output_2(out_8), .in_1(get_instruction_get_inst_1_out_5), .Output_3(out_11),
    .Output_4(out_9), .Output_5(out_12), .out_15(Addi), .out_29(out_24), .out_4(nop), .out_14(Slt),
    .out_17(Slti), .out_31(out_25), .out_6(Add), .out_16(Sltu), .out_19(Sltiu), .out_33(out_26), .out_9(Sub),
    .out_18(And), .out_21(out_33), .out_35(out_27), .out_10(Mul), .out_20(Or), .out_23(out_32),
    .out_37(out_28), .out_11(Mulu), .out_40(Nor), .out_25(out_35), .out_39(out_29), .out_12(Div),
    .out_41(Xor), .out_27(out_23), .out_13(Divu), .out_30(out_20), .out_22(halt), .out_32(out_19),
    .out_24(tty), .out_34(out_30), .out_26(out_34), .out_36(out_21), .out_28(out_37), .out_42(out_31),
    .out_38(out_22));
  or or_10 (Select[0], ALU_Inst, write_inst, R_Inst);
  or or_11 (Select[1], R_Inst, Junp_Inst);
  or or_12 (Select[2], write_inst, memory_inst);
  ALU_Selector alu_selector_1 (
    .in_1(Add), .in_2(Sub), .in_3(Mul), .in_4(Mulu), .in_5(Div), .in_6(Divu), .in_7(Slt), .in_8(Sltu),
    .in_9(And), .in_10(Or), .in_11(Nor), .in_12(Xor), .in_13(Addi), .in_14(Slti), .in_15(Sltiu),
    .in_16(out_33), .in_17(out_32), .in_18(out_35), .Signo(out_16), .I(out_17), .Selector(ALU_Select));
  or or_13 (TTY_enable, out_38, tty);

  // Other names for the same wires on the sheet: Andi = out_33; beq = out_25; bgtz = out_28; blez = out_27;
  //   bltz = out_29; bne = out_26; CLK = in_6; CLR = in_7; const[15:0] = out_9; dest[25:0] = out_8; END = STOP;
  //   Get_Data = out_39; Get_Instruction = out_13; Instruction[31:0] = in_1; j = out_31; jr = out_30; kbd = out_37;
  //   lw = out_23; mfhi = out_21; mflo = out_22; Ori = out_32; Back = out_15; Pc_enable = out_15; pop = out_20;
  //   push = out_19; RD[4:0] = out_12; Ready_Data = in_4; Ready_Inst = in_3; Ready_W = in_2; rnd = out_34;
  //   RS[4:0] = out_10; RT[4:0] = out_11; Start = in_5; sw = out_24; KBD_enable = out_38; tty_1 = out_38;
  //   Write = out_36; Xori = out_35
endmodule

module instruction_decoder (
  input  [31:0] in_1,
  output [4:0] Output,
  output [25:0] Output_2,
  output out_4,
  output [4:0] Output_3,
  output out_6,
  output [15:0] Output_4,
  output [4:0] Output_5,
  output out_9,
  output out_10,
  output out_11,
  output out_12,
  output out_13,
  output out_14,
  output out_15,
  output out_16,
  output out_17,
  output out_18,
  output out_19,
  output out_20,
  output out_21,
  output out_22,
  output out_23,
  output out_24,
  output out_25,
  output out_26,
  output out_27,
  output out_28,
  output out_29,
  output out_30,
  output out_31,
  output out_32,
  output out_33,
  output out_34,
  output out_35,
  output out_36,
  output out_37,
  output out_38,
  output out_39,
  output out_40,
  output out_41,
  output out_42
);

  wire _000000, _111111, comparator_17_eq, comparator_18_eq, comparator_19_eq, comparator_20_eq,
       comparator_21_eq, comparator_22_eq, comparator_23_eq, comparator_24_eq, comparator_25_eq,
       comparator_26_eq, comparator_27_eq, comparator_28_eq, comparator_29_eq, comparator_30_eq,
       comparator_31_eq, comparator_32_eq, comparator_33_eq, comparator_34_eq, comparator_35_eq,
       comparator_36_eq, comparator_37_eq, comparator_38_eq, comparator_39_eq, comparator_40_eq;

  Comparator #(.width(6)) comparator_1 (.a(in_1[31:26]), .b(6'b001000), .eq(out_15));  // open: gt, lt
  Comparator #(.width(6)) comparator_2 (.a(in_1[31:26]), .b(6'b001010), .eq(out_17));  // open: gt, lt
  Comparator #(.width(6)) comparator_3 (.a(in_1[31:26]), .b(6'b001011), .eq(out_19));  // open: gt, lt
  Comparator #(.width(6)) comparator_4 (.a(in_1[31:26]), .b(6'b001100), .eq(out_21));  // open: gt, lt
  Comparator #(.width(6)) comparator_5 (.a(in_1[31:26]), .b(6'b001101), .eq(out_23));  // open: gt, lt
  Comparator #(.width(6)) comparator_6 (.a(in_1[31:26]), .b(6'b001110), .eq(out_25));  // open: gt, lt
  Comparator #(.width(6)) comparator_7 (.a(in_1[31:26]), .b(6'b100011), .eq(out_27));  // open: gt, lt
  Comparator #(.width(6)) comparator_8 (.a(in_1[31:26]), .b(6'b000010), .eq(out_42));  // open: gt, lt
  Comparator #(.width(6)) comparator_9 (.a(in_1[31:26]), .b(6'b101011), .eq(out_29));  // open: gt, lt
  Comparator #(.width(6)) comparator_10 (.a(in_1[31:26]), .b(6'b000100), .eq(out_31));  // open: gt, lt
  Comparator #(.width(6)) comparator_11 (.a(in_1[31:26]), .b(6'b000101), .eq(out_33));  // open: gt, lt
  Comparator #(.width(6)) comparator_12 (.a(in_1[31:26]), .b(6'b000110), .eq(out_35));  // open: gt, lt
  Comparator #(.width(6)) comparator_13 (.a(in_1[31:26]), .b(6'b000111), .eq(out_37));  // open: gt, lt
  Comparator #(.width(6)) comparator_14 (.a(in_1[31:26]), .b(6'b000001), .eq(out_39));  // open: gt, lt
  Comparator #(.width(6)) comparator_15 (.a(in_1[31:26]), .b({6{1'b1}}), .eq(_111111));  // open: gt, lt
  Comparator #(.width(6)) comparator_16 (.a(in_1[31:26]), .b({6{1'b0}}), .eq(_000000));  // open: gt, lt
  Comparator #(.width(6)) comparator_17 (.a(in_1[5:0]), .b({6{1'b0}}), .eq(comparator_17_eq));  // open: gt, lt
  Comparator #(.width(6)) comparator_18 (.a(in_1[5:0]), .b(6'b100000), .eq(comparator_18_eq));  // open: gt, lt
  Comparator #(.width(6)) comparator_19 (.a(in_1[5:0]), .b(6'b100010), .eq(comparator_19_eq));  // open: gt, lt
  Comparator #(.width(6)) comparator_20 (.a(in_1[5:0]), .b(6'b011000), .eq(comparator_20_eq));  // open: gt, lt
  Comparator #(.width(6)) comparator_21 (.a(in_1[5:0]), .b(6'b011001), .eq(comparator_21_eq));  // open: gt, lt
  Comparator #(.width(6)) comparator_22 (.a(in_1[5:0]), .b(6'b011010), .eq(comparator_22_eq));  // open: gt, lt
  Comparator #(.width(6)) comparator_23 (.a(in_1[5:0]), .b(6'b011011), .eq(comparator_23_eq));  // open: gt, lt
  Comparator #(.width(6)) comparator_24 (.a(in_1[5:0]), .b(6'b101010), .eq(comparator_24_eq));  // open: gt, lt
  Comparator #(.width(6)) comparator_25 (.a(in_1[5:0]), .b(6'b000001), .eq(comparator_25_eq));  // open: gt, lt
  Comparator #(.width(6)) comparator_26 (.a(in_1[5:0]), .b(6'b000010), .eq(comparator_26_eq));  // open: gt, lt
  Comparator #(.width(6)) comparator_27 (.a(in_1[31:26]), .b(6'b111000), .eq(comparator_27_eq));  // open: gt, lt
  Comparator #(.width(6)) comparator_28 (.a(in_1[5:0]), .b(6'b000001), .eq(comparator_28_eq));  // open: gt, lt
  and and_1 (out_4, _000000, comparator_17_eq);
  and and_2 (out_6, _000000, comparator_18_eq);
  and and_3 (out_9, _000000, comparator_19_eq);
  and and_4 (out_10, _000000, comparator_20_eq);
  and and_5 (out_11, _000000, comparator_21_eq);
  and and_6 (out_12, _000000, comparator_22_eq);
  and and_7 (out_13, _000000, comparator_23_eq);
  and and_8 (out_14, _000000, comparator_24_eq);
  and and_9 (out_24, _111111, comparator_25_eq);
  and and_10 (out_26, _111111, comparator_26_eq);
  and and_11 (out_32, comparator_27_eq, comparator_28_eq);
  Comparator #(.width(6)) comparator_29 (.a(in_1[5:0]), .b(6'b101011), .eq(comparator_29_eq));  // open: gt, lt
  Comparator #(.width(6)) comparator_30 (.a(in_1[5:0]), .b(6'b100100), .eq(comparator_30_eq));  // open: gt, lt
  Comparator #(.width(6)) comparator_31 (.a(in_1[5:0]), .b(6'b100101), .eq(comparator_31_eq));  // open: gt, lt
  Comparator #(.width(6)) comparator_32 (.a(in_1[5:0]), .b(6'b100111), .eq(comparator_32_eq));  // open: gt, lt
  Comparator #(.width(6)) comparator_33 (.a(in_1[5:0]), .b(6'b101000), .eq(comparator_33_eq));  // open: gt, lt
  Comparator #(.width(6)) comparator_34 (.a(in_1[5:0]), .b(6'b001000), .eq(comparator_34_eq));  // open: gt, lt
  Comparator #(.width(6)) comparator_35 (.a(in_1[5:0]), .b(6'b010000), .eq(comparator_35_eq));  // open: gt, lt
  Comparator #(.width(6)) comparator_36 (.a(in_1[5:0]), .b(6'b010010), .eq(comparator_36_eq));  // open: gt, lt
  Comparator #(.width(6)) comparator_37 (.a(in_1[5:0]), .b({6{1'b1}}), .eq(comparator_37_eq));  // open: gt, lt
  Comparator #(.width(6)) comparator_38 (.a(in_1[5:0]), .b(6'b000100), .eq(comparator_38_eq));  // open: gt, lt
  Comparator #(.width(6)) comparator_39 (.a(in_1[31:26]), .b(6'b111000), .eq(comparator_39_eq));  // open: gt, lt
  Comparator #(.width(6)) comparator_40 (.a(in_1[5:0]), .b({6{1'b0}}), .eq(comparator_40_eq));  // open: gt, lt
  and and_12 (out_16, _000000, comparator_29_eq);
  and and_13 (out_18, _000000, comparator_30_eq);
  and and_14 (out_20, _000000, comparator_31_eq);
  and and_15 (out_40, _000000, comparator_32_eq);
  and and_16 (out_41, _000000, comparator_33_eq);
  and and_17 (out_34, _000000, comparator_34_eq);
  and and_18 (out_36, _000000, comparator_35_eq);
  and and_19 (out_38, _000000, comparator_36_eq);
  and and_20 (out_22, _111111, comparator_37_eq);
  and and_21 (out_28, _111111, comparator_38_eq);
  and and_22 (out_30, comparator_39_eq, comparator_40_eq);

  assign Output = in_1[25:21];
  assign Output_2 = in_1[25:0];
  assign Output_3 = in_1[20:16];
  assign Output_4 = in_1[15:0];
  assign Output_5 = in_1[15:11];

  // Other names for the same wires on the sheet: add = out_6; addi = out_15; and = out_18; andi = out_21;
  //   beq = out_31; bgtz = out_37; blez = out_35; bltz = out_39; bne = out_33; div = out_12; divu = out_13;
  //   halt = out_22; constant[15:0] = in_1[15:0]; dest[25:0] = in_1[25:0]; FC[5:0] = in_1[5:0]; RD[4:0] = in_1[15:11];
  //   RT[4:0] = in_1[20:16]; RS[4:0] = in_1[25:21]; OP[5:0] = in_1[31:26]; j = out_42; jr = out_34; kbd = out_28;
  //   lw = out_27; mfhi = out_36; mflo = out_38; mult = out_10; mulu = out_11; nop = out_4; nor = out_40; or = out_20;
  //   ori = out_23; pop = out_30; push = out_32; rnd = out_26; slt = out_14; slti = out_17; sltiu = out_19;
  //   sltu = out_16; sub = out_9; sw = out_29; tty = out_24; xor = out_41; xori = out_25

  // Notes on the sheet:
  //   Instrucciones Tipo J
  //   Instrucciones Tipo I
  //   Instrucciones Tipo R
endmodule

module Get_Instruction___Get_Inst (
  input  [31:0] in_1,
  input  Load,
  input  CLK,
  input  CLR,
  output [31:0] out_5
);

  Register #(.width(32)) register_1 (
    .D(in_1), .en(Load), .Q({out_5[7:0], out_5[15:8], out_5[23:16], out_5[31:24]}), .clk(CLK), .clr(CLR));

  // Notes on the sheet:
  //   Tomar y guardar la instruccion
endmodule

module RAM_interaction (
  input  [31:0] in_1,
  input  [31:0] in_2,
  input  [31:0] in_3,
  input  [31:0] in_4,
  input  [31:0] in_5,
  input  [3:0] in_6,
  input  [3:0] in_7,
  input  in_8,
  input  in_9,
  input  in_10,
  input  in_11,
  input  in_12,
  input  in_13,
  output [31:0] out_14,
  output [31:0] out_15,
  output [31:0] out_16,
  output [31:0] out_17,
  output [15:0] out_18,
  output [3:0] out_19,
  output out_20,
  output out_21,
  output out_22,
  output out_23,
  output out_24
);

  wire CSD, CSI, or_1_out, Stop;
  wire [31:0] DO0, DO1, DO2, DO3, IO0, IO1, IO2, IO3;

  Multiplexer #(.width(32), .enable("false")) multiplexer_1 (
    .in0({DO0[7:0], DO0[15:8], DO0[23:16], DO0[31:24]}), .in1(IO0), .out(out_14), .sel(in_10));
  Multiplexer #(.width(32), .enable("false")) multiplexer_2 (
    .in0({DO2[7:0], DO2[15:8], DO2[23:16], DO2[31:24]}), .in1(IO2), .out(out_16), .sel(in_10));
  D_Flip_Flop #(.trigger("falling")) d_ff_1 (
    .clk(in_13), .D(in_11), .Q(out_21), .en(or_1_out));  // open: Qn, preset, reset
  or or_1 (or_1_out, in_11, Stop);
  read_RAM read_ram_1 (
    .in_1(in_1), .in_2(in_2), .in_3(in_3), .in_4(in_4), .in_5(in_6), .in_8(in_12), .in_6(in_9), .out_9(IO0),
    .out_10(IO1), .out_11(IO2), .out_12(IO3), .out_14(CSI), .out_13(out_22), .in_7(in_13));
  Cronometro cronometro_1 (.in_2(out_21), .in_3(out_24), .in_4(in_13), .in_1(in_7), .out_5(Stop));
  Multiplexer #(.width(32), .enable("false")) multiplexer_3 (
    .in0({DO1[7:0], DO1[15:8], DO1[23:16], DO1[31:24]}), .in1(IO1), .out(out_15), .sel(in_10));
  Multiplexer #(.width(32), .enable("false")) multiplexer_4 (
    .in0({DO3[7:0], DO3[15:8], DO3[23:16], DO3[31:24]}), .in1(IO3), .out(out_17), .sel(in_10));
  D_Flip_Flop #(.trigger("falling")) d_ff_2 (.clk(in_13), .D(Stop), .Q(out_24));  // open: Qn, preset, en, reset
  read_RAM read_ram_2 (
    .in_1(in_1), .in_2(in_2), .in_3(in_3), .in_4(in_4), .in_5(in_6), .in_8(in_12), .in_6(in_8), .out_9(DO0),
    .out_10(DO1), .out_11(DO2), .out_12(DO3), .out_14(CSD), .out_13(out_23), .in_7(in_13));
  Demultiplexer #(.select(2), .enable("false")) demultiplexer_1 (
    .out0(out_19[0]), .out1(out_19[1]), .out2(out_19[2]), .out3(out_19[3]), .in(1'b1), .sel(in_5[3:2]));
  or or_2 (out_20, CSD, CSI, out_21);

  assign out_18 = in_5[19:4];

  // Other names for the same wires on the sheet: B_0[31:0] = out_14; B_1[31:0] = out_15; B_2[31:0] = out_16;
  //   B_3[31:0] = out_17; Bank_0[31:0] = in_1; Bank_1[31:0] = in_2; Bank_2[31:0] = in_3; Bank_3[31:0] = in_4;
  //   CLK = in_13; CLR = in_12; CS = out_20; DP_address[31:0] = in_5; Address[15:0] = in_5[19:4]; END_Data = out_23;
  //   END_inst = out_22; Escribir = in_11; Get_data = in_8; Get_inst = in_9; Is_inst = in_10; Mask[3:0] = out_19;
  //   ReadT[3:0] = in_6; ready_write = out_24; RW = out_21; WriteT[3:0] = in_7
endmodule

module read_RAM (
  input  [31:0] in_1,
  input  [31:0] in_2,
  input  [31:0] in_3,
  input  [31:0] in_4,
  input  [3:0] in_5,
  input  in_6,
  input  in_7,
  input  in_8,
  output [31:0] out_9,
  output [31:0] out_10,
  output [31:0] out_11,
  output [31:0] out_12,
  output out_13,
  output out_14
);

  wire a, Enable, or_1_out, stop;

  Register #(.width(32)) register_1 (.D(in_1), .en(Enable), .Q(out_9), .clk(in_7), .clr(in_8));
  D_Flip_Flop #(.trigger("falling")) d_ff_1 (.clk(in_7), .D(in_6), .Q(a), .en(or_1_out));  // open: Qn, preset, reset
  or or_1 (or_1_out, in_6, stop);
  Register #(.width(32)) register_2 (.D(in_2), .en(Enable), .Q(out_10), .clk(in_7), .clr(in_8));
  Cronometro cronometro_1 (.in_2(a), .in_3(out_13), .in_4(in_7), .in_1(in_5), .out_5(stop));
  Register #(.width(32)) register_3 (.D(in_3), .en(Enable), .Q(out_11), .clk(in_7), .clr(in_8));
  D_Flip_Flop #(.trigger("falling")) d_ff_2 (.clk(in_7), .D(stop), .Q(Enable), .reset(out_13));  // open: Qn, preset, en
  D_Flip_Flop #(.trigger("falling")) d_ff_3 (.clk(in_7), .D(Enable), .Q(out_13));  // open: Qn, preset, en, reset
  or or_2 (out_14, a, Enable);
  Register #(.width(32)) register_4 (.D(in_4), .en(Enable), .Q(out_12), .clk(in_7), .clr(in_8));

  // Other names for the same wires on the sheet: bank0[31:0] = in_1; bank1[31:0] = in_2; bank2[31:0] = in_3;
  //   bank3[31:0] = in_4; CLK = in_7; CLR = in_8; CS = out_14; Get = in_6; out_bank0[31:0] = out_9;
  //   out_bank1[31:0] = out_10; out_bank2[31:0] = out_11; out_bank3[31:0] = out_12; ready = out_13; RT[3:0] = in_5
endmodule

module Cronometro (
  input  [3:0] in_1,
  input  in_2,
  input  in_3,
  input  in_4,
  output out_5
);

  wire [3:0] counter_1_q;

  Counter #(.width(4), .max('hf)) counter_1 (
    .count(in_2), .Q(counter_1_q), .clk(in_4), .clr(in_3));  // open: load, D, carry
  Comparator #(.width(4)) comparator_1 (.a(in_1), .b(counter_1_q), .eq(out_5));  // open: gt, lt

  // Other names for the same wires on the sheet: Aumentar = in_2; CLK = in_4; CLR = in_3;
  //   Tiempo_de_espera[3:0] = in_1
endmodule
